# Fritzing sketch SLG_pushbutton_0.7 (saved by Fritzing 0.6.2b)
breadboards: 1

parts:
  B2-2 = female pin header, 1 pin [form="♀ (female)"]
  B1-2 = female pin header, 1 pin [form="♀ (female)"]
  B2+2 = female pin header, 1 pin [form="♀ (female)"]
  B1+2 = female pin header, 1 pin [form="♀ (female)"]
  Vin2 = female pin header, 1 pin [form="♀ (female)"]
  Tc5 = female pin header, 1 pin [form="♀ (female)"]
  Tc6 = female pin header, 1 pin [form="♀ (female)"]
  Tcr2 = female pin header, 1 pin [form="♀ (female)"]
  Rt2 = Resistor [resistance=1k tolerance=±5% package=THT]
  B7 = female pin header, 1 pin [form="♀ (female)"]
  B8 = female pin header, 1 pin [form="♀ (female)"]
  B9 = female pin header, 1 pin [form="♀ (female)"]
  S7 = Pushbutton [package="[THT]"]
  S8 = Pushbutton [package="[THT]"]
  S9 = Pushbutton [package="[THT]"]
  Rs7 = Resistor [resistance=10k tolerance=±5% package=THT]
  Rs8 = Resistor [resistance=10k tolerance=±5% package=THT]
  Rs9 = Resistor [resistance=10k tolerance=±5% package=THT]

nets:
  N1: B2-2.pin1, B1-2.pin1, Tc6.pin1, Rs7.Pin_0, Rs8.Pin_0, Rs9.Pin_0
  N2: B2+2.pin1, B1+2.pin1, Vin2.pin1
  N3: Tc5.pin1, Tcr2.pin1, Rt2.Pin_0
  N4: Rt2.Pin_1, S7.Pin_1, S7.Pin_2, S8.Pin_1, S8.Pin_2, S9.Pin_1, S9.Pin_2
  N5: B7.pin1, S7.Pin_3, S7.Pin_4, Rs9.Pin_1
  N6: B8.pin1, S8.Pin_3, S8.Pin_4, Rs8.Pin_1
  N7: B9.pin1, S9.Pin_3, S9.Pin_4, Rs7.Pin_1
