# Fritzing sketch SolarLogMeter_main_0.7 (saved by Fritzing 0.6.2b)
breadboards: 1

parts:
  AD5206 = AD5206 Digital Potentiometer [package="DIP28 [THT]"]
  R1 = Resistor [resistance=10k tolerance=±5% package=THT]
  R1b = Resistor [resistance=10k tolerance=±5% package=THT]
  R2b = Resistor [resistance=10k tolerance=±5% package=THT]
  V2H = female pin header, 1 pin [form="♀ (female)"]
  SC2+ = female pin header, 1 pin [form="♀ (female)"]
  Ri1 = Resistor [resistance=100k tolerance=±5% package=THT]
  Ri1b = Resistor [resistance=1k tolerance=±5% package=THT]
  Ri2b = Resistor [resistance=1k tolerance=±5% package=THT]
  Vi1 = female pin header, 1 pin [form="♀ (female)"]
  Ri2 = Resistor [resistance=100k tolerance=±5% package=THT]
  Vi2 = female pin header, 1 pin [form="♀ (female)"]
  A52 = female pin header, 1 pin [form="♀ (female)"]
  A51 = female pin header, 1 pin [form="♀ (female)"]
  A53 = female pin header, 1 pin [form="♀ (female)"]
  SC1- = female pin header, 1 pin [form="♀ (female)"]
  SC2- = female pin header, 1 pin [form="♀ (female)"]
  V1H = female pin header, 1 pin [form="♀ (female)"]
  GND = female pin header, 1 pin [form="♀ (female)"]
  5+ = female pin header, 1 pin [form="♀ (female)"]
  V1L = female pin header, 1 pin [form="♀ (female)"]
  V2L = female pin header, 1 pin [form="♀ (female)"]
  SC1+ = female pin header, 1 pin [form="♀ (female)"]
  A42 = female pin header, 1 pin [form="♀ (female)"]
  R2 = Resistor [resistance=10k tolerance=±5% package=THT]
  Tr3 = transistor_signal_NPN_IRF520
  Tr4 = transistor_signal_NPN_IRF520
  U1 = LM 358 Dual Op-Amp [package="DIP8 [THT]"]

nets:
  N1: AD5206.A6, AD5206.A2, AD5206.A4, Tr4.connector2
  N2: AD5206.W6, AD5206.W2, AD5206.W4, U1.connector2
  GND: AD5206.B6, AD5206.Gnd, AD5206.Vss, AD5206.B5, AD5206.B3, AD5206.B1, AD5206.B2, AD5206.B4, R1b.Pin_0, R2b.Pin_0, Ri1b.Pin_1, Ri2b.Pin_0, SC1-.pin1, SC2-.pin1, GND.pin1, U1.connector3
  N3: AD5206.CS, A53.pin1
  N4: AD5206.Vdd, 5+.pin1, U1.connector7
  N5: AD5206.SDI, A51.pin1
  N6: AD5206.CLK, A52.pin1
  N7: AD5206.W5, AD5206.W3, AD5206.W1, U1.connector4
  N8: AD5206.A5, AD5206.A3, AD5206.A1, Tr3.connector2
  N9: R1.Pin_0, V1L.pin1, SC1+.pin1, Tr3.connector1
  N10: R1.Pin_1, R1b.Pin_1, V1H.pin1
  N11: R2b.Pin_1, V2H.pin1, R2.Pin_0
  N12: SC2+.pin1, V2L.pin1, R2.Pin_1, Tr4.connector1
  N13: Ri1.Pin_0, Ri1b.Pin_0, U1.connector5
  N14: Ri1.Pin_1, Vi1.pin1, U1.connector6
  N15: Ri2b.Pin_1, Ri2.Pin_0, U1.connector1
  N16: Ri2.Pin_1, Vi2.pin1, U1.connector0
  N17: A42.pin1, Tr3.connector0, Tr4.connector0

notes:
  SolarLogMeter
  v. 0.7 - 20110813
