# Fritzing sketch SolarLogMeter_0.6 (saved by Fritzing 0.5.2b)
breadboards: 1

parts:
  AD5206 = AD5206 Digital Potentiometer [package="DIP28 [THT]"]
  R1 = Resistor [resistance=10k package=THT]
  R1b = Resistor [resistance=10k package=THT]
  R2b = Resistor [resistance=10k package=THT]
  V2H = female pin header, 1 pin [form="♀ (female)"]
  SC2+ = female pin header, 1 pin [form="♀ (female)"]
  TS922 = lm358
  Ri1 = Resistor [resistance=100k package=THT]
  Ri1b = Resistor [resistance=1k package=THT]
  Ri2b = Resistor [resistance=1k package=THT]
  Vi1 = female pin header, 1 pin [form="♀ (female)"]
  Ri2 = Resistor [resistance=100k package=THT]
  Vi2 = female pin header, 1 pin [form="♀ (female)"]
  A52 = female pin header, 1 pin [form="♀ (female)"]
  A51 = female pin header, 1 pin [form="♀ (female)"]
  A53 = female pin header, 1 pin [form="♀ (female)"]
  SC1- = female pin header, 1 pin [form="♀ (female)"]
  SC2- = female pin header, 1 pin [form="♀ (female)"]
  V1H = female pin header, 1 pin [form="♀ (female)"]
  GND = female pin header, 1 pin [form="♀ (female)"]
  5+ = female pin header, 1 pin [form="♀ (female)"]
  S1 = Pushbutton [package="[THT]"]
  S2 = Pushbutton [package="[THT]"]
  S3 = Pushbutton [package="[THT]"]
  Rs3 = Resistor [resistance=10k package=THT]
  B1 = female pin header, 1 pin [form="♀ (female)"]
  B2 = female pin header, 1 pin [form="♀ (female)"]
  B3 = female pin header, 1 pin [form="♀ (female)"]
  Rs2 = Resistor [resistance=10k package=THT]
  Rs1 = Resistor [resistance=10k package=THT]
  V1L = female pin header, 1 pin [form="♀ (female)"]
  V2L = female pin header, 1 pin [form="♀ (female)"]
  SC1+ = female pin header, 1 pin [form="♀ (female)"]
  Tr1 = transistor_signal_NPN_IRF520
  A42 = female pin header, 1 pin [form="♀ (female)"]
  R2 = Resistor [resistance=10k package=THT]
  Tr2 = transistor_signal_NPN_IRF520
  Rt = Resistor [resistance=1k package=THT]
  Tcr = female pin header, 1 pin [form="♀ (female)"]
  Tc2 = female pin header, 1 pin [form="♀ (female)"]
  Tc1 = female pin header, 1 pin [form="♀ (female)"]
  Vin = female pin header, 1 pin [form="♀ (female)"]
  B1+ = female pin header, 1 pin [form="♀ (female)"]
  B2+ = female pin header, 1 pin [form="♀ (female)"]
  B1- = female pin header, 1 pin [form="♀ (female)"]
  B2- = female pin header, 1 pin [form="♀ (female)"]

nets:
  N1: AD5206.A6, AD5206.A2, AD5206.A4, Tr2.connector2
  N2: AD5206.W6, AD5206.W2, AD5206.W4, TS922.connector2
  GND: AD5206.B6, AD5206.Gnd, AD5206.Vss, AD5206.B5, AD5206.B3, AD5206.B1, AD5206.B2, AD5206.B4, R1b.Pin_0, R2b.Pin_0, TS922.connector3, Ri1b.Pin_1, Ri2b.Pin_0, SC1-.pin1, SC2-.pin1, GND.pin1, Rs3.Pin_0, Rs2.Pin_0, Rs1.Pin_0, Tc2.pin1, B1-.pin1, B2-.pin1
  N3: AD5206.CS, A53.pin1
  N4: AD5206.Vdd, TS922.connector7, 5+.pin1, S1.Pin_1, S1.Pin_2, S2.Pin_1, S2.Pin_2, S3.Pin_1, S3.Pin_2, Rt.Pin_1
  N5: AD5206.SDI, A51.pin1
  N6: AD5206.CLK, A52.pin1
  N7: AD5206.W5, AD5206.W3, AD5206.W1, TS922.connector4
  N8: AD5206.A5, AD5206.A3, AD5206.A1, Tr1.connector2
  N9: R1.Pin_0, V1L.pin1, SC1+.pin1, Tr1.connector1
  N10: R1.Pin_1, R1b.Pin_1, V1H.pin1
  N11: R2b.Pin_1, V2H.pin1, R2.Pin_0
  N12: SC2+.pin1, V2L.pin1, R2.Pin_1, Tr2.connector1
  N13: TS922.connector0, Ri2.Pin_1, Vi2.pin1
  N14: TS922.connector1, Ri2b.Pin_1, Ri2.Pin_0
  N15: TS922.connector5, Ri1.Pin_0, Ri1b.Pin_0
  N16: TS922.connector6, Ri1.Pin_1, Vi1.pin1
  N17: S1.Pin_3, S1.Pin_4, B1.pin1, Rs1.Pin_1
  N18: S2.Pin_3, S2.Pin_4, B2.pin1, Rs2.Pin_1
  N19: S3.Pin_3, S3.Pin_4, Rs3.Pin_1, B3.pin1
  N20: Tr1.connector0, A42.pin1, Tr2.connector0
  N21: Rt.Pin_0, Tcr.pin1, Tc1.pin1
  N22: Vin.pin1, B1+.pin1, B2+.pin1

notes:
  v. 0.3 - 20110609
  SolarLogMeter
